# Fritzing sketch Day_06_Add Pot (saved by Fritzing 1.0.0rc)
breadboards: 3

parts:
  Part1 = Arduino Mega 2560 (Rev3)
  interiorLightsButton = Pushbutton [package="[SMD]"]
  R2 = Resistor [tolerance=±5% power=0.25W resistance=100 package=THT]
  batteryStatusLight = smd LED [color="Red (633nm)" package="1206 [SMD]"]
  R3 = Resistor [tolerance=±5% power=0.25W resistance=220 package=THT]
  R4 = Resistor [tolerance=±5% power=0.25W resistance=220 package=THT]
  solarArray = PHOTOCELL [package=photocell-kit]
  R6 = Resistor [tolerance=±5% power=0.25W resistance=200 package=THT]
  R7 = Resistor [tolerance=±5% power=0.25W resistance=220 package=THT]
  interiorLighting = smd LED [color="White (4500K)" package="0603 [SMD]"]
  Mod1 = Passive Buzzer
  R8 = Trimmer Potentiometer [maximum_resistance=10kΩ knob_status=50% power=0.5W package=THT]

nets:
  N1: Part1.A15, R8.wiper
  N2: Part1.GND, R7.Pin_0, interiorLighting.cathode, Mod1.-
  N3: Part1.D13_PWM, Mod1.S
  N4: Part1.5V, interiorLightsButton.Pin_1, interiorLightsButton.Pin_2, R2.Pin_0, solarArray.P$2, R8.leg1, R8.leg2
  N5: Part1.D22, solarArray.P$1, R7.Pin_1
  N6: Part1.D24, interiorLightsButton.Pin_3, interiorLightsButton.Pin_4, R2.Pin_1
  N7: Part1.D26, R3.Pin_1
  N8: Part1.D27, R4.Pin_1
  N9: batteryStatusLight.cathode, R4.Pin_0
  N10: batteryStatusLight.anode, R3.Pin_0
  N11: R6.Pin_0, interiorLighting.anode
